# Fritzing sketch ThHum_meter1 (saved by Fritzing 0.9.6b)
circuit board: 3.5cm x 6cm
breadboards: 1

parts:
  WeMos_D1_Mini1 = WeMos D1 Mini
  R2 = Resistor [tolerance=±5% power=0.25 resistance=220 package=THT]
  R1 = Resistor [tolerance=±5% power=0.25 resistance=220 package=THT]
  R3 = Resistor [tolerance=±5% power=0.25 resistance=220 package=THT]
  R4 = Resistor [tolerance=±5% power=0.25 resistance=220 package=THT]
  J3 = male pin header, 4 pins [form="♂ (male)"]
  J1 = male pin header, 2 pins [form="♂ (male)"]
  J2 = male pin header, 2 pins [form="♂ (male)"]
  J4 = male pin header, 3 pins [form="♂ (male)"]
  J5 = male pin header, 3 pins [form="♂ (male)"]
  J7 = male pin header, 8 pins [form="♂ (male)"]
  J6 = male pin header, 8 pins [form="♂ (male)"]
  J8 = male pin header, 2 pins [form="♂ (male)"]
  D2 = Rectifier Diode [part_number=1N4148 package="300 mil [THT]"]
  D1 = Rectifier Diode [part_number=1N4148 package="300 mil [THT]"]

nets:
  3.3V: WeMos_D1_Mini1.3V3, R3.Pin_0, R4.Pin_0, J3.pin1, J4.pin1, J5.pin1, J6.pin1, D1.cathode
  N1: WeMos_D1_Mini1.5V, J7.pin1
  N2: WeMos_D1_Mini1.A0, R1.Pin_0, J6.pin7
  N3: WeMos_D1_Mini1.D0, WeMos_D1_Mini1.D5, J6.pin5, J6.pin6, D2.cathode
  N4: WeMos_D1_Mini1.D1, R3.Pin_1, J3.pin4, J7.pin6
  N5: WeMos_D1_Mini1.D2, R4.Pin_1, J3.pin3, J7.pin5
  N6: WeMos_D1_Mini1.D3, J7.pin4
  N7: WeMos_D1_Mini1.D4, J7.pin3
  N8: WeMos_D1_Mini1.D6, J6.pin4
  N9: WeMos_D1_Mini1.D7, J6.pin3, J8.pin2
  N10: WeMos_D1_Mini1.D8, J6.pin2
  GND: WeMos_D1_Mini1.G, R2.Pin_1, J3.pin2, J1.pin1, J2.pin1, J4.pin2, J5.pin2, J7.pin2, J8.pin1
  N11: WeMos_D1_Mini1.RST, J6.pin8, D2.anode
  N12: WeMos_D1_Mini1.RX, J7.pin7
  N13: WeMos_D1_Mini1.TX, J7.pin8
  N14: R2.Pin_0, R1.Pin_1, J2.pin2
  N15: J1.pin2, D1.anode
  N16: J4.pin3, J5.pin3

notes:
  zf221114.1750
  zf221114.1013
  i2c/1-wire
  ADC
  dsleep
  step-up 5V
  bat Li-Ion
  GND
  +
  OUT-GND-IN
  3.3V-GND-SDA-SCL
  GND-IN
